# Fritzing sketch Untitled Sketch 2 (saved by Fritzing 0.9.3b)
breadboards: 1

parts:
  Part1 = Arduino Micro (Rev3)  # not connected
  S1 = Round Pushbutton
  S2 = Round Pushbutton
  S3 = Round Pushbutton
  U1 = POT [package=pot_alpha_rv16af-20]
  U2 = POT [package=pot_alpha_rv16af-20]

nets:
  N1: S1.leg1, S2.leg1, S3.leg1, U1.E, U2.E
  N2: U1.A, U2.A
